// Logisim project branch_control.circ as structural Verilog: 2 circuits, main circuit branch_control
module branch_control (
  input  [31:0] PC_in,
  input  jump,
  input  flag,
  input  [15:0] offset,
  input  [25:0] constant,
  input  [31:0] R_s,
  input  J,
  input  JR,
  output [31:0] PC_out
);

  wire jump_t;
  wire [27:0] pc;
  wire [31:0] bit_extender_1_out, multiplexer_1_out, multiplier_1_out, sum;
  wire [31:28] dest;

  assign bit_extender_1_out = {{16{offset[15]}}, offset};  // Bit_Extender bit_extender_1
  Multiplier #(.width(32)) multiplier_1 (.a(bit_extender_1_out), .b(32'h4), .out(multiplier_1_out));  // open: cin, cout
  Adder #(.width(32)) adder_1 (.a(PC_in), .b(32'h4), .out({dest, pc}));  // open: cin, cout
  Multiplexer #(.width(32), .enable("false")) multiplexer_1 (
    .in0({dest, pc}), .in1(sum), .out(multiplexer_1_out), .sel(jump_t));
  and and_1 (jump_t, jump, flag);
  // Probe on sum
  Adder #(.width(32)) adder_2 (.a({dest, pc}), .b(multiplier_1_out), .out(sum));  // open: cin, cout
  // Probe on multiplier_1_out
  Multiplexer #(.select(2), .width(32)) multiplexer_2 (
    .in0(multiplexer_1_out), .in1({dest, constant, 2'b00}), .in2(R_s), .out(PC_out), .sel({JR, J}));  // open: in3, en

  // Other names for the same wires on the sheet: dest[27:2] = constant; pc[31:28] = dest; hypothesis = flag;
  //   if = jump

  // Notes on the sheet:
  //   Direccion de la
  //   Instruccion Actual
  //   Instruccion de Salto
  //   Condicion de Salto
  //   Tamanno de Salto (k)
  //   tamanno de palabra
  //   Direccion de la
  //   Proxima Instruccion
endmodule

module test (
  input  [31:0] in_1,
  input  in_2,
  input  in_3,
  input  [15:0] in_4,
  output [31:0] out_5
);

  // Probe on in_1
  // Probe on in_4
  branch_control branch_control_1 (
    .PC_in(in_1), .jump(in_2), .flag(in_3), .offset(in_4), .PC_out(out_5));  // open: J, JR, constant, R_s
  // Probe on out_5
endmodule
