// Logisim project instruction_decoder.circ as structural Verilog: 11 circuits, main circuit instruction_decoder
module instruction_decoder (
  input  [31:0] instruction,
  output [5:0] op_code,
  output [4:0] Rs,
  output [4:0] Rt,
  output [4:0] Rd,
  output [5:0] func_code,
  output [31:0] constant,
  output [25:0] jump,
  output [3:0] alu_selector,
  output immediate,
  output [1:0] d_in_selector,
  output data_path_rw,
  output halt,
  output comparisiion,
  output is_jump,
  output is_copy,
  output is_on_memory,
  output LW,
  output POP,
  output [15:0] offset
);

  wire comparator_1_eq, comparator_2_eq, is_arit_logic, is_logic_1_s1, logic_imm, not_1_out, not_2_out,
       not_is_jump, or_1_out;
  wire [3:0] alu_s_imm, alu_s_reg, alu_selector_t;
  wire [31:0] bit_extender_1_out, bit_extender_2_out;

  alu_selector_translator alu_selector_translator_1 (
    .a(instruction[5]), .b(instruction[4]), .c(instruction[3]), .d(instruction[2]), .e(instruction[1]),
    .f(instruction[0]), .s1(alu_s_reg[3]), .s2(alu_s_reg[2]), .s3(alu_s_reg[1]), .s4(alu_s_reg[0]));
  not not_1 (not_1_out, instruction[30]);
  and and_1 (immediate, instruction[29], not_1_out, not_2_out);
  not not_2 (not_2_out, instruction[31]);
  Multiplexer #(.width(2)) multiplexer_1 (.in0(2'b00), .in1(2'b01), .out(d_in_selector), .sel(or_1_out));  // open: en
  or or_1 (or_1_out, comparisiion, POP, LW, is_copy);
  assign bit_extender_1_out = {{16{instruction[15]}}, instruction[15:0]};  // Bit_Extender bit_extender_1
  assign bit_extender_2_out = {{16{1'b0}}, instruction[15:0]};  // Bit_Extender bit_extender_2
  Multiplexer #(.enable("false")) multiplexer_2 (.in0(1'b0), .in1(1'b1), .out(data_path_rw), .sel(not_is_jump));
  immediate_translator immediate_translator_1 (
    .a1(instruction[26]), .a2(instruction[27]), .a3(instruction[28]), .s1(alu_s_imm[3]), .s2(alu_s_imm[2]),
    .s3(alu_s_imm[1]), .s4(alu_s_imm[0]));
  is_logic is_logic_1 (
    .a4(alu_selector_t[3]), .a3(alu_selector_t[2]), .a2(alu_selector_t[1]), .a1(alu_selector_t[0]),
    .s1(is_logic_1_s1));
  Multiplexer #(.width(32), .enable("false")) multiplexer_3 (
    .in0(bit_extender_1_out), .in1(bit_extender_2_out), .out(constant), .sel(logic_imm));
  and and_2 (logic_imm, immediate, is_logic_1_s1);
  Comparator #(.width(6)) comparator_1 (.a({6{1'b1}}), .b(instruction[5:0]), .eq(comparator_1_eq));  // open: gt, lt
  Multiplexer #(.width(4), .enable("false")) multiplexer_4 (
    .in0(alu_s_reg), .in1(alu_s_imm), .out(alu_selector_t), .sel(immediate));
  Comparator #(.width(6)) comparator_2 (
    .a(instruction[31:26]), .b(instruction[5:0]), .eq(comparator_2_eq));  // open: gt, lt
  and and_3 (halt, comparator_2_eq, comparator_1_eq);
  Multiplexer #(.width(4), .enable("false")) multiplexer_5 (
    .in0(alu_selector_t), .in1(4'b0000), .out(alu_selector), .sel(is_jump));
  comparission_detector comparission_detector_1 (
    .Op0(instruction[26]), .Op1(instruction[27]), .Op2(instruction[28]), .Op3(instruction[29]),
    .Op4(instruction[30]), .Op5(instruction[31]), .F0(instruction[0]), .F1(instruction[1]),
    .F2(instruction[2]), .F3(instruction[3]), .F4(instruction[4]), .F5(instruction[5]), .COMP(comparisiion));
  jump_detector jump_detector_1 (
    .Op0(instruction[26]), .Op1(instruction[27]), .Op2(instruction[28]), .Op3(instruction[29]),
    .Op4(instruction[30]), .Op5(instruction[31]), .F0(instruction[0]), .F1(instruction[1]),
    .F2(instruction[2]), .F3(instruction[3]), .F4(instruction[4]), .F5(instruction[5]), .is_jump(is_jump));
  copy_detector copy_detector_1 (
    .OP0(instruction[26]), .OP1(instruction[27]), .OP2(instruction[28]), .OP3(instruction[29]),
    .OP4(instruction[30]), .OP5(instruction[31]), .F0(instruction[0]), .F1(instruction[1]),
    .F2(instruction[2]), .F3(instruction[3]), .F4(instruction[4]), .F5(instruction[5]), .is_copy(is_copy));
  on_memory_detector on_memory_detector_1 (
    .OP0(instruction[26]), .OP1(instruction[27]), .OP2(instruction[28]), .OP3(instruction[29]),
    .OP4(instruction[30]), .OP5(instruction[31]), .F0(instruction[0]), .F1(instruction[1]),
    .F2(instruction[2]), .F3(instruction[3]), .F4(instruction[4]), .F5(instruction[5]),
    .is_on_memory(is_on_memory), .LW(LW), .POP(POP));
  or or_2 (not_is_jump, comparisiion, is_copy, is_on_memory, immediate, is_arit_logic);
  aritmetic_detector aritmetic_detector_1 (
    .OP0(instruction[26]), .OP1(instruction[27]), .OP2(instruction[28]), .OP3(instruction[29]),
    .OP4(instruction[30]), .OP5(instruction[31]), .F0(instruction[0]), .F1(instruction[1]),
    .F2(instruction[2]), .F3(instruction[3]), .F4(instruction[4]), .F5(instruction[5]),
    .is_aritmetic(is_arit_logic));

  assign func_code = instruction[5:0];
  assign jump = instruction[25:0];
  assign offset = instruction[15:0];
  assign op_code = instruction[31:26];
  assign Rd = instruction[15:11];
  assign Rs = instruction[25:21];
  assign Rt = instruction[20:16];

  // Other names for the same wires on the sheet: alu_final[3:0] = alu_selector; comparission = comparisiion;
  //   full_constant[31:0] = constant; constant_t[15:0] = instruction[15:0]; x[4:0] = instruction[10:6];
  //   register_d[4:0] = instruction[15:11]; register_t[4:0] = instruction[20:16];
  //   register_s[4:0] = instruction[25:21]

  // Notes on the sheet:
  //   001 <=> immediate
  //   000 <=> no wait
endmodule

module alu_selector_translator (
  input  a,
  input  b,
  input  c,
  input  d,
  input  e,
  input  f,
  output s1,
  output s2,
  output s3,
  output s4
);

  wire and_1_out, and_2_out, and_4_out, and_5_out, and_6_out, and_7_out, and_8_out, and_9_out, and_10_out,
       not_1_out, not_2_out, not_3_out, not_4_out, not_5_out, not_6_out, not_7_out, not_8_out, not_9_out,
       not_10_out, not_11_out;

  not not_1 (not_1_out, f);
  not not_2 (not_2_out, e);
  not not_3 (not_3_out, d);
  not not_4 (not_4_out, b);
  not not_5 (not_5_out, b);
  not not_6 (not_6_out, e);
  not not_7 (not_7_out, b);
  not not_8 (not_8_out, d);
  not not_9 (not_9_out, d);
  not not_10 (not_10_out, e);
  not not_11 (not_11_out, f);
  and and_1 (and_1_out, d, e);
  and and_2 (and_2_out, c, not_1_out);
  and and_3 (s2, d, not_2_out);
  and and_4 (and_4_out, not_3_out, f);
  and and_5 (and_5_out, d, e);
  and and_6 (and_6_out, not_4_out, c);
  and and_7 (and_7_out, not_5_out, not_6_out, f);
  and and_8 (and_8_out, not_7_out, not_8_out, e);
  and and_9 (and_9_out, not_9_out, e, f);
  and and_10 (and_10_out, c, not_10_out, not_11_out);
  or or_1 (s1, and_1_out, and_2_out);
  or or_2 (s3, and_4_out, and_5_out, and_6_out);
  or or_3 (s4, and_7_out, and_8_out, and_9_out, and_10_out);
endmodule

module d_in_selector (
  input  immediate,
  output s1,
  output s2
);


  assign s1 = immediate;
  assign s2 = 1'b0;
endmodule

module immediate_translator (
  input  a1,
  input  a2,
  input  a3,
  output s1,
  output s2,
  output s3,
  output s4
);

  wire and_2_out;

  and and_1 (s1, a1, a2);
  or or_1 (s2, a3, a1);
  and and_2 (and_2_out, a1, a3);
  or or_2 (s4, a2, and_2_out);

  assign s3 = 1'b0;
endmodule

module test_instruction (
);

  wire data_path_1_p10, data_path_1_p11, data_path_1_p12, data_path_1_p13, data_path_1_p14, data_path_1_p15,
       immediate, rw;
  wire [1:0] data_selector;
  wire [3:0] alu_selector;
  wire [4:0] register_d, register_s, register_t, x;
  wire [5:0] func_code, op_code;
  wire [25:0] jump;
  wire [31:0] constant, ram;

  // Probe on {6{1'b0}}
  // Probe on 6'b001000
  // Probe on 32'h20620020
  instruction_decoder instruction_decoder_1 (
    .op_code(op_code), .Rs(register_s), .Rt(register_t), .Rd(register_d), .func_code(func_code),
    .constant(constant), .jump(jump), .alu_selector(alu_selector), .immediate(immediate),
    .d_in_selector(data_selector), .data_path_rw(rw));  // open: instruction, halt, comparisiion, is_jump, is_copy, is_on_memory, LW, POP, offset
  // Probe on register_d
  // Probe on register_t
  // Probe on register_s
  // Probe on op_code
  // Probe on func_code
  // Probe on x
  // data_path data_path_1: pin names not known; wires that end beside it: register_t, register_d, register_s, rw, constant, ram, alu_selector, data_selector, immediate, data_path_1_p10, data_path_1_p11, data_path_1_p12, data_path_1_p13, data_path_1_p14, data_path_1_p15
  // Probe on constant

  // Notes on the sheet:
  //   instructions
  //   constant
  //   registers
  //   register
  //   instant
  //   idem
endmodule

module comparission_detector (
  input  Op0,
  input  Op1,
  input  Op2,
  input  Op3,
  input  Op4,
  input  Op5,
  input  F0,
  input  F1,
  input  F2,
  input  F3,
  input  F4,
  input  F5,
  output COMP
);

  wire and_1_out, and_2_out, and_3_out, not_1_out, not_2_out, not_3_out, not_4_out, not_5_out, not_6_out,
       not_7_out, not_8_out, not_9_out, not_10_out, not_11_out, not_12_out, not_13_out, not_14_out,
       not_15_out, not_16_out, not_17_out, not_18_out, not_19_out;

  not not_1 (not_1_out, Op0);
  not not_2 (not_2_out, Op1);
  not not_3 (not_3_out, Op2);
  not not_4 (not_4_out, Op3);
  not not_5 (not_5_out, Op4);
  not not_6 (not_6_out, Op5);
  not not_7 (not_7_out, F2);
  not not_8 (not_8_out, F4);
  not not_9 (not_9_out, Op0);
  not not_10 (not_10_out, Op1);
  not not_11 (not_11_out, Op2);
  not not_12 (not_12_out, Op3);
  not not_13 (not_13_out, Op4);
  not not_14 (not_14_out, F2);
  not not_15 (not_15_out, F4);
  not not_16 (not_16_out, Op0);
  not not_17 (not_17_out, Op2);
  not not_18 (not_18_out, Op4);
  not not_19 (not_19_out, Op5);
  and and_1 (and_1_out, not_1_out, not_2_out, not_3_out, not_4_out, not_5_out, not_6_out, F1, not_7_out, F3, not_8_out, F5);
  and and_2 (and_2_out, not_9_out, not_10_out, not_11_out, not_12_out, not_13_out, F0, F1, not_14_out, F3, not_15_out, F5);
  and and_3 (and_3_out, not_16_out, Op1, not_17_out, Op3, not_18_out, not_19_out);
  or or_1 (COMP, and_1_out, and_2_out, and_3_out);
endmodule

module jump_detector (
  input  Op0,
  input  Op1,
  input  Op2,
  input  Op3,
  input  Op4,
  input  Op5,
  input  F0,
  input  F1,
  input  F2,
  input  F3,
  input  F4,
  input  F5,
  output is_jump
);

  wire and_1_out, and_2_out, and_3_out, and_4_out, not_1_out, not_2_out, not_3_out, not_4_out, not_5_out,
       not_6_out, not_7_out, not_8_out, not_9_out, not_10_out, not_11_out, not_12_out, not_13_out,
       not_14_out, not_15_out, not_16_out, not_17_out, not_18_out, not_19_out, not_20_out;

  not not_1 (not_1_out, Op0);
  not not_2 (not_2_out, Op3);
  not not_3 (not_3_out, Op4);
  not not_4 (not_4_out, Op5);
  not not_5 (not_5_out, F0);
  not not_6 (not_6_out, F1);
  not not_7 (not_7_out, F2);
  not not_8 (not_8_out, F4);
  not not_9 (not_9_out, F5);
  not not_10 (not_10_out, Op3);
  not not_11 (not_11_out, Op4);
  not not_12 (not_12_out, Op5);
  not not_13 (not_13_out, Op0);
  not not_14 (not_14_out, Op3);
  not not_15 (not_15_out, Op4);
  not not_16 (not_16_out, Op5);
  not not_17 (not_17_out, Op1);
  not not_18 (not_18_out, Op3);
  not not_19 (not_19_out, Op4);
  not not_20 (not_20_out, Op5);
  and and_1 (and_1_out, not_1_out, not_2_out, not_3_out, not_4_out, not_5_out, not_6_out, not_7_out, F3, not_8_out, not_9_out);
  and and_2 (and_2_out, Op2, not_10_out, not_11_out, not_12_out);
  and and_3 (and_3_out, not_13_out, Op1, not_14_out, not_15_out, not_16_out);
  and and_4 (and_4_out, Op0, not_17_out, not_18_out, not_19_out, not_20_out);
  or or_1 (is_jump, and_1_out, and_2_out, and_3_out, and_4_out);
endmodule

module copy_detector (
  input  OP0,
  input  OP1,
  input  OP2,
  input  OP3,
  input  OP4,
  input  OP5,
  input  F0,
  input  F1,
  input  F2,
  input  F3,
  input  F4,
  input  F5,
  output is_copy
);

  wire not_1_out, not_2_out, not_3_out, not_4_out, not_5_out, not_6_out, not_7_out, not_8_out, not_9_out,
       not_10_out;

  not not_1 (not_1_out, OP0);
  not not_2 (not_2_out, OP1);
  not not_3 (not_3_out, OP2);
  not not_4 (not_4_out, OP3);
  not not_5 (not_5_out, OP4);
  not not_6 (not_6_out, OP5);
  not not_7 (not_7_out, F0);
  not not_8 (not_8_out, F2);
  not not_9 (not_9_out, F3);
  not not_10 (not_10_out, F5);
  and and_1 (is_copy, not_1_out, not_2_out, not_3_out, not_4_out, not_5_out, not_6_out, not_7_out, not_8_out, not_9_out, F4, not_10_out);
endmodule

module on_memory_detector (
  input  OP0,
  input  OP1,
  input  OP2,
  input  OP3,
  input  OP4,
  input  OP5,
  input  F0,
  input  F1,
  input  F2,
  input  F3,
  input  F4,
  input  F5,
  output is_on_memory,
  output LW,
  output POP
);

  wire and_1_out, and_2_out, not_1_out, not_2_out, not_3_out, not_4_out, not_5_out, not_6_out, not_7_out,
       not_8_out, not_9_out, not_10_out, not_11_out, not_12_out, not_13_out, not_14_out, not_15_out,
       not_16_out, not_17_out, not_18_out, not_19_out, not_20_out, not_21_out, not_22_out;

  not not_1 (not_1_out, OP0);
  not not_2 (not_2_out, OP1);
  not not_3 (not_3_out, OP2);
  not not_4 (not_4_out, F1);
  not not_5 (not_5_out, F2);
  not not_6 (not_6_out, F3);
  not not_7 (not_7_out, F4);
  not not_8 (not_8_out, F5);
  not not_9 (not_9_out, OP2);
  not not_10 (not_10_out, OP4);
  not not_11 (not_11_out, OP2);
  not not_12 (not_12_out, OP3);
  not not_13 (not_13_out, OP4);
  not not_14 (not_14_out, OP0);
  not not_15 (not_15_out, OP1);
  not not_16 (not_16_out, OP2);
  not not_17 (not_17_out, F0);
  not not_18 (not_18_out, F1);
  not not_19 (not_19_out, F2);
  not not_20 (not_20_out, F3);
  not not_21 (not_21_out, F4);
  not not_22 (not_22_out, F5);
  and and_1 (and_1_out, not_1_out, not_2_out, not_3_out, OP3, OP4, OP5, not_4_out, not_5_out, not_6_out, not_7_out, not_8_out);
  and and_2 (and_2_out, OP0, OP1, not_9_out, not_10_out, OP5);
  and and_3 (LW, OP0, OP1, not_11_out, not_12_out, not_13_out, OP5);
  and and_4 (POP, not_14_out, not_15_out, not_16_out, OP3, OP4, OP5, not_17_out, not_18_out, not_19_out, not_20_out, not_21_out, not_22_out);
  or or_1 (is_on_memory, and_1_out, and_2_out);
endmodule

module aritmetic_detector (
  input  OP0,
  input  OP1,
  input  OP2,
  input  OP3,
  input  OP4,
  input  OP5,
  input  F0,
  input  F1,
  input  F2,
  input  F3,
  input  F4,
  input  F5,
  output is_aritmetic
);

  wire and_1_out, and_2_out, and_3_out, and_4_out, and_5_out, not_1_out, not_2_out, not_3_out, not_4_out,
       not_5_out, not_6_out, not_7_out, not_8_out, not_9_out, not_10_out, not_11_out, not_12_out, not_13_out,
       not_14_out, not_15_out, not_16_out, not_17_out, not_18_out, not_19_out, not_20_out, not_21_out,
       not_22_out, not_23_out, not_24_out, not_25_out, not_26_out, not_27_out, not_28_out, not_29_out,
       not_30_out, not_31_out, not_32_out, not_33_out, not_34_out, not_35_out, not_36_out, not_37_out,
       not_38_out, not_39_out, not_40_out, not_41_out, not_42_out, not_43_out, not_44_out, not_45_out,
       not_46_out, not_47_out;

  not not_1 (not_1_out, OP0);
  not not_2 (not_2_out, OP1);
  not not_3 (not_3_out, OP2);
  not not_4 (not_4_out, OP3);
  not not_5 (not_5_out, OP4);
  not not_6 (not_6_out, OP5);
  not not_7 (not_7_out, F0);
  not not_8 (not_8_out, F1);
  not not_9 (not_9_out, F3);
  not not_10 (not_10_out, F4);
  not not_11 (not_11_out, OP0);
  not not_12 (not_12_out, OP1);
  not not_13 (not_13_out, OP2);
  not not_14 (not_14_out, OP3);
  not not_15 (not_15_out, OP4);
  not not_16 (not_16_out, OP5);
  not not_17 (not_17_out, F0);
  not not_18 (not_18_out, F2);
  not not_19 (not_19_out, F3);
  not not_20 (not_20_out, F4);
  not not_21 (not_21_out, OP0);
  not not_22 (not_22_out, OP1);
  not not_23 (not_23_out, OP2);
  not not_24 (not_24_out, OP3);
  not not_25 (not_25_out, OP4);
  not not_26 (not_26_out, OP5);
  not not_27 (not_27_out, F1);
  not not_28 (not_28_out, F3);
  not not_29 (not_29_out, F4);
  not not_30 (not_30_out, OP0);
  not not_31 (not_31_out, OP1);
  not not_32 (not_32_out, OP2);
  not not_33 (not_33_out, OP3);
  not not_34 (not_34_out, OP4);
  not not_35 (not_35_out, OP5);
  not not_36 (not_36_out, F3);
  not not_37 (not_37_out, F4);
  not not_38 (not_38_out, OP0);
  not not_39 (not_39_out, OP1);
  not not_40 (not_40_out, OP2);
  not not_41 (not_41_out, OP3);
  not not_42 (not_42_out, OP4);
  not not_43 (not_43_out, OP5);
  not not_44 (not_44_out, F0);
  not not_45 (not_45_out, F1);
  not not_46 (not_46_out, F2);
  not not_47 (not_47_out, F4);
  and and_1 (and_1_out, not_1_out, not_2_out, not_3_out, not_4_out, not_5_out, not_6_out, not_7_out, not_8_out, not_9_out, not_10_out, F5);
  and and_2 (and_2_out, not_11_out, not_12_out, not_13_out, not_14_out, not_15_out, not_16_out, not_17_out, not_18_out, not_19_out, not_20_out, F5);
  and and_3 (and_3_out, not_21_out, not_22_out, not_23_out, not_24_out, not_25_out, not_26_out, F0, not_27_out, F2, not_28_out, not_29_out, F5);
  and and_4 (and_4_out, not_30_out, not_31_out, not_32_out, not_33_out, not_34_out, not_35_out, F0, F1, F2, not_36_out, not_37_out, F5);
  and and_5 (and_5_out, not_38_out, not_39_out, not_40_out, not_41_out, not_42_out, not_43_out, not_44_out, not_45_out, not_46_out, F3, not_47_out, F5);
  or or_1 (is_aritmetic, and_1_out, and_2_out, and_3_out, and_4_out, and_5_out);
endmodule

module is_logic (
  input  a4,
  input  a3,
  input  a2,
  input  a1,
  output s1
);

  wire and_1_out, and_2_out, not_1_out, not_2_out, not_3_out;

  not not_1 (not_1_out, a4);
  and and_1 (and_1_out, not_1_out, a3, not_2_out);
  not not_2 (not_2_out, a2);
  and and_2 (and_2_out, a4, not_3_out, a2);
  not not_3 (not_3_out, a3);
  or or_1 (s1, and_1_out, and_2_out);
endmodule
